# Fritzing sketch transmitter (saved by Fritzing 0.9.3b)
circuit board: 8.46667cm x 5.64444cm
breadboards: 1

parts:
  Part1 = Arduino Uno (Rev3)
  Part2 = Adafruit RFM69HCW Transceiver Radio [part_number="Adafruit #3070 and #3071"]
  10K = POT [package=pot_alpha_rv16af-20]

nets:
  N1: Part1.A0, 10K.S
  N2: Part1.D11_PWM/MOSI, Part2.MOSI
  N3: Part1.D12/MISO, Part2.MISO
  N4: Part1.D13/SCK, Part2.SCK
  GND: Part1.GND, Part2.GND, 10K.E
  N5: Part1.D2, Part2.RST
  N6: Part1.D3_PWM, Part2.DIO0
  N7: Part1.D4, Part2.CS
  N8: Part2.DIO1, Part2.DIO2, Part2.DIO3, Part2.DIO4
  N9: Part2.VIN, 10K.A

custom parts:
  Adafruit RFM69HCW Transceiver Radio: Sending data over long distances is like magic, and now you can be a magician with this range of powerful and easy-to-use radio modules. Sure, sometimes you want to talk to a computer (a good time to use WiFi) or perhaps communicate with a Phone (choose Bluetooth Low Energy!) but what if you want to send data very far? Most WiFi, Bluetooth, Zigbee and other wireless chipsets use 2.4GHz, which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
